// Logisim project NanoSwitch16.circ as structural Verilog: 3 circuits, main circuit main
module main (
  output _0110,
  output _0111
);

  wire adder_1_y, adder_2_x, adder_2_y, adder_3_x, adder_3_y, adder_4_x, adder_4_y, and_1_out, and_2_out,
       and_3_out, and_4_out, and_5_out, and_6_out, and_7_out, and_8_out, and_9_out, and_10_out, and_11_out,
       and_12_out, and_13_out, and_14_out, and_15_out, and_16_out, and_17_out, and_18_out, and_19_out,
       and_20_out, and_21_out, and_22_out, and_23_out, and_24_out, and_25_out, and_26_out, and_27_out,
       and_28_out, and_29_out, and_30_out, and_31_out, and_32_out, and_33_out, and_34_out, and_35_out,
       and_36_out, and_37_out, and_38_out, and_39_out, and_40_out, and_41_out, and_42_out, and_43_out,
       and_44_out, and_45_out, and_46_out, and_47_out, and_48_out, and_49_out, and_50_out, and_51_out,
       and_52_out, and_53_out, and_54_out, and_55_out, and_56_out, and_57_out, and_58_out, and_59_out,
       and_60_out, and_61_out, and_62_out, and_63_out, and_64_out, and_65_out, and_66_out, and_67_out,
       and_68_out, and_69_out, and_70_out, and_71_out, and_72_out, and_73_out, and_74_out, and_75_out,
       and_76_out, and_77_out, and_78_out, and_79_out, and_80_out, and_81_out, and_82_out, and_83_out,
       and_84_out, and_85_out, and_86_out, and_87_out, and_90_out, and_91_out, and_92_out, and_93_out,
       and_94_out, clock_pulse, d_ff_13_qn, d_ff_14_q, d_ff_15_q, d_ff_16_q, d_ff_16_qn, d_ff_21_q,
       d_ff_22_q, d_ff_23_q, d_ff_24_q, d_ff_25_q, d_ff_26_q, d_ff_27_q, d_ff_28_q, d_ff_33_q, d_ff_34_q,
       d_ff_35_q, execute_puls_out, fetch, full_adder_1_out_4, full_adder_1_out_5, full_adder_2_out_4,
       full_adder_2_out_5, full_adder_3_out_4, full_adder_3_out_5, full_adder_4_out_4, full_adder_4_out_5,
       not_1_out, not_2_out, not_3_out, not_4_out, not_5_out, not_6_out, not_7_out, not_8_out, not_9_out,
       not_10_out, not_11_out, not_12_out, not_13_out, not_14_out, not_15_out, not_16_out, not_17_out,
       not_18_out, not_19_out, or_1_out, or_2_out, or_7_out, or_8_out, or_9_out, or_10_out, or_11_out,
       or_12_out, or_13_out, or_14_out, or_15_out, or_24_out, or_25_out, or_42_out, or_43_out;
  wire [3:0] d_ff_1_q, d_ff_5_q, d_ff_12_q, d_ff_17_q, d_ff_29_q, d_ff_39_q, or_3_out, or_26_out, or_35_out;
  wire [7:0] or_16_out, or_41_out, ram_1_dout;

  Clock clock_1 (.out(clock_pulse));
  D_Flip_Flop d_ff_1 (.D(d_ff_29_q[0]), .clk(or_1_out), .Q(d_ff_1_q[0]));  // open: Qn, preset, reset
  D_Flip_Flop d_ff_2 (.D(d_ff_29_q[1]), .clk(or_1_out), .Q(d_ff_1_q[1]));  // open: Qn, preset, reset
  D_Flip_Flop d_ff_3 (.D(d_ff_29_q[2]), .clk(or_1_out), .Q(d_ff_1_q[2]));  // open: Qn, preset, reset
  D_Flip_Flop d_ff_4 (.D(d_ff_29_q[3]), .clk(or_1_out), .Q(d_ff_1_q[3]));  // open: Qn, preset, reset
  D_Flip_Flop d_ff_5 (.D(d_ff_29_q[0]), .clk(and_90_out), .Q(d_ff_5_q[0]));  // open: Qn, preset, reset
  D_Flip_Flop d_ff_6 (.D(d_ff_29_q[1]), .clk(and_90_out), .Q(d_ff_5_q[1]));  // open: Qn, preset, reset
  D_Flip_Flop d_ff_7 (.D(d_ff_29_q[2]), .clk(and_90_out), .Q(d_ff_5_q[2]));  // open: Qn, preset, reset
  D_Flip_Flop d_ff_8 (.D(d_ff_29_q[3]), .clk(and_90_out), .Q(d_ff_5_q[3]));  // open: Qn, preset, reset
  or or_1 (or_1_out, and_91_out, and_92_out);
  D_Flip_Flop d_ff_9 (.D(d_ff_21_q), .clk(d_ff_13_qn), .Q(d_ff_12_q[3]));  // open: Qn, preset, reset
  D_Flip_Flop d_ff_10 (.D(d_ff_22_q), .clk(d_ff_13_qn), .Q(d_ff_12_q[2]));  // open: Qn, preset, reset
  D_Flip_Flop d_ff_11 (.D(d_ff_23_q), .clk(d_ff_13_qn), .Q(d_ff_12_q[1]));  // open: Qn, preset, reset
  D_Flip_Flop d_ff_12 (.D(d_ff_24_q), .clk(d_ff_13_qn), .Q(d_ff_12_q[0]));  // open: Qn, preset, reset
  and execute_puls (execute_puls_out, clock_pulse, fetch);
  not not_1 (not_1_out, fetch);
  and and_1 (and_1_out, clock_pulse, not_3_out);
  not not_2 (not_2_out, and_1_out);
  not not_3 (not_3_out, d_ff_14_q);
  and and_2 (and_2_out, fetch, and_84_out);
  not not_4 (not_4_out, clock_pulse);
  and and_3 (and_3_out, fetch, and_83_out);
  D_Flip_Flop d_ff_13 (.D(not_1_out), .clk(not_2_out), .Q(fetch), .Qn(d_ff_13_qn));  // open: preset, reset
  D_Flip_Flop d_ff_14 (.D(and_2_out), .clk(not_4_out), .Q(d_ff_14_q));  // open: Qn, preset, reset
  D_Flip_Flop d_ff_15 (.D(or_2_out), .clk(not_5_out), .Q(d_ff_15_q));  // open: Qn, preset, reset
  or or_2 (or_2_out, or_43_out, and_3_out);
  not not_5 (not_5_out, clock_pulse);
  and and_4 (and_4_out, or_16_out[4], d_ff_16_q);
  and and_5 (and_5_out, or_16_out[5], d_ff_16_q);
  and and_6 (and_6_out, or_16_out[6], d_ff_16_q);
  and and_7 (and_7_out, or_16_out[7], d_ff_16_q);
  not not_6 (not_6_out, and_84_out);
  and and_8 (and_8_out, d_ff_1_q[0], fetch);
  and and_9 (and_9_out, d_ff_1_q[1], fetch);
  and and_10 (and_10_out, d_ff_1_q[2], fetch);
  and and_11 (and_11_out, d_ff_1_q[3], fetch);
  and and_12 (and_12_out, d_ff_5_q[0], d_ff_13_qn);
  and and_13 (and_13_out, d_ff_5_q[1], d_ff_13_qn);
  and and_14 (and_14_out, d_ff_5_q[2], d_ff_13_qn);
  and and_15 (and_15_out, d_ff_5_q[3], d_ff_13_qn);
  and and_16 (and_16_out, or_16_out[0], d_ff_16_qn);
  and and_17 (and_17_out, or_16_out[1], d_ff_16_qn);
  and and_18 (and_18_out, or_16_out[2], d_ff_16_qn);
  and and_19 (and_19_out, or_16_out[3], d_ff_16_qn);
  and and_20 (and_20_out, fetch, not_6_out);
  and and_21 (and_21_out, clock_pulse, not_7_out);
  not not_7 (not_7_out, and_2_out);
  or or_3 (or_3_out[0], and_8_out, and_12_out);
  or or_4 (or_3_out[1], and_9_out, and_13_out);
  or or_5 (or_3_out[2], and_10_out, and_14_out);
  or or_6 (or_3_out[3], and_11_out, and_15_out);
  adder adder_1 (.a(d_ff_12_q[3]), .b(adder_2_x), .y(adder_1_y));  // open: x
  adder adder_2 (.a(d_ff_12_q[2]), .b(adder_3_x), .x(adder_2_x), .y(adder_2_y));
  adder adder_3 (.a(d_ff_12_q[1]), .b(adder_4_x), .x(adder_3_x), .y(adder_3_y));
  adder adder_4 (.a(d_ff_12_q[0]), .b(1'b1), .x(adder_4_x), .y(adder_4_y));
  RAM ram_1 (
    .addr({or_3_out, or_26_out}), .we(d_ff_14_q), .oe(not_8_out), .clk(or_7_out), .din(or_41_out),
    .dout(ram_1_dout));
  not not_8 (not_8_out, d_ff_14_q);
  or or_7 (or_7_out, and_21_out, d_ff_14_q);
  D_Flip_Flop d_ff_16 (.D(and_91_out), .clk(or_1_out), .Q(d_ff_16_q), .Qn(d_ff_16_qn));  // open: preset, reset
  D_Flip_Flop d_ff_17 (.D(or_8_out), .clk(d_ff_15_q), .Q(d_ff_17_q[0]));  // open: Qn, preset, reset
  or or_8 (or_8_out, and_16_out, and_4_out);
  D_Flip_Flop d_ff_18 (.D(or_9_out), .clk(d_ff_15_q), .Q(d_ff_17_q[1]));  // open: Qn, preset, reset
  or or_9 (or_9_out, and_17_out, and_5_out);
  D_Flip_Flop d_ff_19 (.D(or_10_out), .clk(d_ff_15_q), .Q(d_ff_17_q[2]));  // open: Qn, preset, reset
  or or_10 (or_10_out, and_18_out, and_6_out);
  D_Flip_Flop d_ff_20 (.D(or_11_out), .clk(d_ff_15_q), .Q(d_ff_17_q[3]));  // open: Qn, preset, reset
  or or_11 (or_11_out, and_19_out, and_7_out);
  not not_9 (not_9_out, or_42_out);
  and and_22 (and_22_out, not_9_out, adder_1_y);
  and and_23 (and_23_out, not_9_out, adder_2_y);
  and and_24 (and_24_out, not_9_out, adder_3_y);
  and and_25 (and_25_out, not_9_out, adder_4_y);
  or or_12 (or_12_out, and_22_out, and_26_out);
  and and_26 (and_26_out, or_42_out, d_ff_29_q[3]);
  or or_13 (or_13_out, and_23_out, and_27_out);
  and and_27 (and_27_out, or_42_out, d_ff_29_q[2]);
  or or_14 (or_14_out, and_24_out, and_28_out);
  and and_28 (and_28_out, or_42_out, d_ff_29_q[1]);
  or or_15 (or_15_out, and_25_out, and_29_out);
  and and_29 (and_29_out, or_42_out, d_ff_29_q[0]);
  not not_10 (not_10_out, clock_pulse);
  or or_16 (or_16_out[0], and_35_out, and_39_out);
  or or_17 (or_16_out[1], and_36_out, and_40_out);
  or or_18 (or_16_out[2], and_37_out, and_41_out);
  or or_19 (or_16_out[3], and_38_out, and_42_out);
  or or_20 (or_16_out[4], and_35_out, and_43_out);
  or or_21 (or_16_out[5], and_36_out, and_44_out);
  or or_22 (or_16_out[6], and_37_out, and_45_out);
  or or_23 (or_16_out[7], and_38_out, and_46_out);
  not not_11 (not_11_out, and_85_out);
  not not_12 (not_12_out, and_90_out);
  D_Flip_Flop d_ff_21 (.D(and_30_out), .clk(clock_pulse), .Q(d_ff_21_q));  // open: Qn, preset, reset
  and and_30 (and_30_out, not_12_out, or_12_out);
  D_Flip_Flop d_ff_22 (.D(and_31_out), .clk(clock_pulse), .Q(d_ff_22_q));  // open: Qn, preset, reset
  and and_31 (and_31_out, not_12_out, or_13_out);
  D_Flip_Flop d_ff_23 (.D(and_32_out), .clk(clock_pulse), .Q(d_ff_23_q));  // open: Qn, preset, reset
  and and_32 (and_32_out, not_12_out, or_14_out);
  D_Flip_Flop d_ff_24 (.D(and_33_out), .clk(clock_pulse), .Q(d_ff_24_q));  // open: Qn, preset, reset
  and and_33 (and_33_out, not_12_out, or_15_out);
  and and_34 (and_34_out, and_20_out, not_10_out);
  and and_35 (and_35_out, d_ff_39_q[0], or_43_out);
  and and_36 (and_36_out, d_ff_39_q[1], or_43_out);
  and and_37 (and_37_out, d_ff_39_q[2], or_43_out);
  and and_38 (and_38_out, d_ff_39_q[3], or_43_out);
  and and_39 (and_39_out, ram_1_dout[0], not_13_out);
  and and_40 (and_40_out, ram_1_dout[1], not_13_out);
  and and_41 (and_41_out, ram_1_dout[2], not_13_out);
  and and_42 (and_42_out, ram_1_dout[3], not_13_out);
  and and_43 (and_43_out, ram_1_dout[4], not_13_out);
  and and_44 (and_44_out, ram_1_dout[5], not_13_out);
  and and_45 (and_45_out, ram_1_dout[6], not_13_out);
  and and_46 (and_46_out, ram_1_dout[7], not_13_out);
  and and_47 (and_47_out, not_11_out, d_ff_16_q);
  and and_48 (and_48_out, not_11_out, d_ff_16_qn);
  and and_49 (and_49_out, and_85_out, d_ff_16_qn);
  or or_24 (or_24_out, and_48_out, and_50_out);
  and and_50 (and_50_out, and_85_out, d_ff_16_q);
  not not_13 (not_13_out, or_43_out);
  or or_25 (or_25_out, and_47_out, and_49_out);
  and and_51 (and_51_out, ram_1_dout[4], or_24_out);
  and and_52 (and_52_out, ram_1_dout[5], or_24_out);
  and and_53 (and_53_out, ram_1_dout[6], or_24_out);
  and and_54 (and_54_out, ram_1_dout[7], or_24_out);
  or or_26 (or_26_out[0], and_62_out, and_66_out);
  or or_27 (or_26_out[1], and_63_out, and_67_out);
  or or_28 (or_26_out[2], and_64_out, and_68_out);
  or or_29 (or_26_out[3], and_65_out, and_69_out);
  or or_30 (or_41_out[7], and_55_out, and_75_out);
  and and_55 (and_55_out, or_25_out, d_ff_17_q[3]);
  D_Flip_Flop d_ff_25 (.D(ram_1_dout[4]), .clk(and_34_out), .Q(d_ff_25_q));  // open: Qn, preset, reset
  D_Flip_Flop d_ff_26 (.D(ram_1_dout[5]), .clk(and_34_out), .Q(d_ff_26_q));  // open: Qn, preset, reset
  D_Flip_Flop d_ff_27 (.D(ram_1_dout[6]), .clk(and_34_out), .Q(d_ff_27_q));  // open: Qn, preset, reset
  D_Flip_Flop d_ff_28 (.D(ram_1_dout[7]), .clk(and_34_out), .Q(d_ff_28_q));  // open: Qn, preset, reset
  D_Flip_Flop d_ff_29 (.D(ram_1_dout[0]), .clk(and_34_out), .Q(d_ff_29_q[0]));  // open: Qn, preset, reset
  D_Flip_Flop d_ff_30 (.D(ram_1_dout[1]), .clk(and_34_out), .Q(d_ff_29_q[1]));  // open: Qn, preset, reset
  D_Flip_Flop d_ff_31 (.D(ram_1_dout[2]), .clk(and_34_out), .Q(d_ff_29_q[2]));  // open: Qn, preset, reset
  D_Flip_Flop d_ff_32 (.D(ram_1_dout[3]), .clk(and_34_out), .Q(d_ff_29_q[3]));  // open: Qn, preset, reset
  or or_31 (or_41_out[6], and_56_out, and_76_out);
  or or_32 (or_41_out[5], and_57_out, and_77_out);
  and and_56 (and_56_out, or_25_out, d_ff_17_q[2]);
  and and_57 (and_57_out, or_25_out, d_ff_17_q[1]);
  and and_58 (and_58_out, ram_1_dout[0], or_25_out);
  and and_59 (and_59_out, ram_1_dout[1], or_25_out);
  and and_60 (and_60_out, ram_1_dout[2], or_25_out);
  and and_61 (and_61_out, ram_1_dout[3], or_25_out);
  and and_62 (and_62_out, d_ff_12_q[0], not_14_out);
  and and_63 (and_63_out, d_ff_12_q[1], not_14_out);
  and and_64 (and_64_out, d_ff_12_q[2], not_14_out);
  and and_65 (and_65_out, d_ff_12_q[3], not_14_out);
  not not_14 (not_14_out, fetch);
  and and_66 (and_66_out, d_ff_29_q[0], fetch);
  and and_67 (and_67_out, d_ff_29_q[1], fetch);
  and and_68 (and_68_out, d_ff_29_q[2], fetch);
  and and_69 (and_69_out, d_ff_29_q[3], fetch);
  or or_33 (or_41_out[4], and_70_out, and_79_out);
  or or_34 (or_41_out[3], and_71_out, and_80_out);
  and and_70 (and_70_out, or_25_out, d_ff_17_q[0]);
  and and_71 (and_71_out, or_25_out, or_35_out[3]);
  or or_35 (or_35_out[0], and_58_out, and_51_out);
  or or_36 (or_35_out[1], and_59_out, and_52_out);
  or or_37 (or_35_out[2], and_60_out, and_53_out);
  or or_38 (or_35_out[3], and_61_out, and_54_out);
  or or_39 (or_41_out[2], and_72_out, and_81_out);
  or or_40 (or_41_out[1], and_73_out, and_82_out);
  and and_72 (and_72_out, or_25_out, or_35_out[2]);
  and and_73 (and_73_out, or_25_out, or_35_out[1]);
  not not_15 (not_15_out, d_ff_28_q);
  or or_41 (or_41_out[0], and_74_out, and_93_out);
  and and_74 (and_74_out, or_25_out, or_35_out[0]);
  and and_75 (and_75_out, or_24_out, or_35_out[3]);
  not not_16 (not_16_out, d_ff_27_q);
  and and_76 (and_76_out, or_24_out, or_35_out[2]);
  and and_77 (and_77_out, or_24_out, or_35_out[1]);
  not not_17 (not_17_out, d_ff_26_q);
  not not_18 (not_18_out, d_ff_25_q);
  and and_78 (and_78_out, fetch, and_85_out);
  not not_19 (not_19_out, clock_pulse);
  and and_79 (and_79_out, or_24_out, or_35_out[0]);
  and and_80 (and_80_out, or_24_out, d_ff_17_q[3]);
  D_Flip_Flop d_ff_33 (.D(and_78_out), .clk(not_19_out), .Q(d_ff_33_q));  // open: Qn, preset, reset
  and and_81 (and_81_out, or_24_out, d_ff_17_q[2]);
  and and_82 (and_82_out, or_24_out, d_ff_17_q[1]);
  and and_83 (and_83_out, d_ff_25_q, not_17_out, execute_puls_out, not_16_out, not_15_out);
  and and_84 (and_84_out, not_18_out, d_ff_26_q, execute_puls_out, not_16_out, not_15_out);
  and and_85 (and_85_out, d_ff_25_q, d_ff_26_q, execute_puls_out, not_16_out, not_15_out);
  and and_86 (and_86_out, not_18_out, not_17_out, d_ff_27_q, not_15_out);
  and and_87 (and_87_out, d_ff_25_q, not_17_out, d_ff_27_q, not_15_out);
  and and_88 (_0110, not_18_out, d_ff_26_q, execute_puls_out, d_ff_27_q, not_15_out);
  and and_89 (_0111, d_ff_25_q, d_ff_26_q, execute_puls_out, d_ff_27_q, not_15_out);
  and and_90 (and_90_out, not_18_out, not_17_out, execute_puls_out, not_16_out, d_ff_28_q);
  and and_91 (and_91_out, d_ff_25_q, not_17_out, execute_puls_out, not_16_out, d_ff_28_q);
  and and_92 (and_92_out, not_18_out, d_ff_26_q, execute_puls_out, not_16_out, d_ff_28_q);
  D_Flip_Flop d_ff_34 (.D(d_ff_33_q), .clk(clock_pulse), .Q(d_ff_34_q));  // open: Qn, preset, reset
  and and_93 (and_93_out, or_24_out, d_ff_17_q[0]);
  full_adder full_adder_1 (
    .in_1(or_35_out[3]), .in_2(d_ff_17_q[3]), .in_3(full_adder_2_out_4), .out_4(full_adder_1_out_4),
    .out_5(full_adder_1_out_5));
  full_adder full_adder_2 (
    .in_1(or_35_out[2]), .in_2(d_ff_17_q[2]), .in_3(full_adder_3_out_4), .out_4(full_adder_2_out_4),
    .out_5(full_adder_2_out_5));
  full_adder full_adder_3 (
    .in_1(or_35_out[1]), .in_2(d_ff_17_q[1]), .in_3(full_adder_4_out_4), .out_4(full_adder_3_out_4),
    .out_5(full_adder_3_out_5));
  full_adder full_adder_4 (
    .in_1(or_35_out[0]), .in_2(d_ff_17_q[0]), .out_4(full_adder_4_out_4), .out_5(full_adder_4_out_5));  // open: in_3
  or or_42 (or_42_out, and_86_out, and_94_out);
  and and_94 (and_94_out, and_87_out, d_ff_35_q);
  D_Flip_Flop d_ff_35 (.D(full_adder_1_out_4), .clk(or_43_out), .Q(d_ff_35_q));  // open: Qn, preset, reset
  D_Flip_Flop d_ff_36 (.D(full_adder_1_out_5), .clk(or_43_out), .Q(d_ff_39_q[3]));  // open: Qn, preset, reset
  D_Flip_Flop d_ff_37 (.D(full_adder_2_out_5), .clk(or_43_out), .Q(d_ff_39_q[2]));  // open: Qn, preset, reset
  D_Flip_Flop d_ff_38 (.D(full_adder_3_out_5), .clk(or_43_out), .Q(d_ff_39_q[1]));  // open: Qn, preset, reset
  D_Flip_Flop d_ff_39 (.D(full_adder_4_out_5), .clk(or_43_out), .Q(d_ff_39_q[0]));  // open: Qn, preset, reset
  or or_43 (or_43_out, d_ff_33_q, d_ff_34_q);

  // Notes on the sheet:
  //   fetch register
  //   write signal
  //   ram page
  //   program page
  //   enable write to a register
  //   delay write signal 
  //   a register
  //   ram side register
  //   reset
  //   opcode
  //   operand
  //   Instruction register
  //   store a register
  //   use Operand as address
  //   instruction decoder
  //   NOP
  //   LDA
  //   STA
  //   ADD
  //   JMP
  //   CMP
  //   PJP
  //   RSU
  //   RSL
endmodule

module adder (
  input  a,
  input  b,
  output x,
  output y
);

  wire and_2_out, and_3_out, not_1_out, not_2_out;

  not not_1 (not_1_out, a);
  not not_2 (not_2_out, b);
  and and_1 (x, a, b);
  and and_2 (and_2_out, a, not_2_out);
  and and_3 (and_3_out, not_1_out, b);
  or or_1 (y, and_2_out, and_3_out);
endmodule

module full_adder (
  input  in_1,
  input  in_2,
  input  in_3,
  output out_4,
  output out_5
);

  wire and_1_out, and_2_out, and_3_out;

  and and_1 (and_1_out, in_1, in_2);
  and and_2 (and_2_out, in_1, in_3);
  and and_3 (and_3_out, in_2, in_3);
  ExactlyOne xor_1 (.out(out_5), .in0(in_1), .in1(in_2), .in2(in_3));
  or or_1 (out_4, and_1_out, and_2_out, and_3_out);
endmodule
